// Logisim project RISCVDatapathLogisim.circ as structural Verilog: 11 circuits, main circuit RISCV_DataPath
module RISCV_DataPath (
);

  wire clock_1_out, controllogic_1_auipc, controllogic_1_branch, controllogic_1_databselect,
       controllogic_1_immselect, controllogic_1_jal, controllogic_1_jalr, controllogic_1_lui,
       controllogic_1_memread, controllogic_1_memtoreg, controllogic_1_memwrite, controllogic_1_regwrite,
       controllogic_1_type_s, fuctionlogic_1_sub_en, programcounter_1_wmux;
  wire [1:0] fuctionlogic_1_storeselect;
  wire [2:0] fuctionlogic_1_loadselect;
  wire [3:0] fuctionlogic_1_aluop;
  wire [4:0] controllogic_1_controlop;
  wire [6:0] ram_1_data;
  wire [23:0] programcounter_1_instruction_count;
  wire [24:0] ram_1_data_2;
  wire [31:0] dataselect_1_data_w, immediategen_1_imm32bit, loadtype_1_dataw, multiplexer_1_out,
       multiplexer_2_out, n32bitalu_1_output, programcounter_1_nextinstcount, ram_2_data, registermemory_1_a,
       registermemory_1_b, storetype_1_memd;

  ProgramCounter programcounter_1 (
    .Instruction_Count(programcounter_1_instruction_count), .JAL(controllogic_1_jal), .ImmCode(ram_1_data_2),
    .NextInstCount(programcounter_1_nextinstcount), .WMux(programcounter_1_wmux), .JALR(controllogic_1_jalr),
    .ALUData(loadtype_1_dataw), .AUPIC(controllogic_1_auipc), .Branch(controllogic_1_branch));
  RAM #(.addrWidth(24), .dataWidth(32)) ram_1 (
    .addr(programcounter_1_instruction_count), .data({ram_1_data_2, ram_1_data}));  // open: sel, clk, ld, clr
  DataSelect dataselect_1 (
    .ALUData(loadtype_1_dataw), .NextInstCount(programcounter_1_nextinstcount),
    .InstCode({ram_1_data_2, ram_1_data}), .Data_W(dataselect_1_data_w), .WMux(programcounter_1_wmux),
    .LUI(controllogic_1_lui));
  ControlLogic controllogic_1 (
    .Opcode(ram_1_data), .MemWrite(controllogic_1_memwrite), .MemRead(controllogic_1_memread),
    .MemToReg(controllogic_1_memtoreg), .RegWrite(controllogic_1_regwrite),
    .DataBSelect(controllogic_1_databselect), .ControlOp(controllogic_1_controlop),
    .ImmSelect(controllogic_1_immselect), .Type_S(controllogic_1_type_s), .JAL(controllogic_1_jal),
    .JALR(controllogic_1_jalr), .AUIPC(controllogic_1_auipc), .LUI(controllogic_1_lui),
    .Branch(controllogic_1_branch));
  RegisterMemory registermemory_1 (
    .WriteData(dataselect_1_data_w), .A(registermemory_1_a), .B(registermemory_1_b),
    .Write_Register(ram_1_data_2[4:0]), .RegWrite(controllogic_1_regwrite),
    .Read_Register_B(ram_1_data_2[17:13]), .Read_Register_A(ram_1_data_2[12:8]));
  ImmediateGen immediategen_1 (
    .Imm32Bit(immediategen_1_imm32bit), .ImmSelect(controllogic_1_immselect), .Imm25Bit(ram_1_data_2),
    .Type_S(controllogic_1_type_s));
  Multiplexer #(.width(32)) multiplexer_1 (
    .in0(registermemory_1_b), .in1(immediategen_1_imm32bit), .out(multiplexer_1_out),
    .sel(controllogic_1_databselect));  // open: en
  FuctionLogic fuctionlogic_1 (
    .ALUFunction(ram_1_data_2[7:5]), .FunctionCode(ram_1_data_2[24:18]), .Sub_EN(fuctionlogic_1_sub_en),
    .ALUOp(fuctionlogic_1_aluop), .ControlOp(controllogic_1_controlop),
    .LoadSelect(fuctionlogic_1_loadselect), .StoreSelect(fuctionlogic_1_storeselect));
  _32BitALU u_32bitalu_1 (
    .A(registermemory_1_a), .B(multiplexer_1_out), .Sub_EN(fuctionlogic_1_sub_en),
    .ALUOp(fuctionlogic_1_aluop), .Output(n32bitalu_1_output));  // open: Overflow, Zero
  StoreType storetype_1 (.Data_rs2(registermemory_1_b), .MemD(storetype_1_memd), .StoreSel(fuctionlogic_1_storeselect));
  Clock clock_1 (.out(clock_1_out));
  RAM #(.addrWidth(24), .dataWidth(32), .bus("separate")) ram_2 (
    .addr(n32bitalu_1_output[23:0]), .din(storetype_1_memd), .data(ram_2_data),
    .str(controllogic_1_memwrite), .clk(clock_1_out), .ld(controllogic_1_memread));  // open: sel, clr
  Multiplexer #(.width(32)) multiplexer_2 (
    .in0(n32bitalu_1_output), .in1(ram_2_data), .out(multiplexer_2_out), .sel(controllogic_1_memtoreg));  // open: en
  LoadType loadtype_1 (.DMem(multiplexer_2_out), .DataW(loadtype_1_dataw), .LoadSel(fuctionlogic_1_loadselect));

  // Notes on the sheet:
  //   Instruction Memory
  //   RISC-V Architecture Datapath
  //   Direct Memory
endmodule

module RegisterMemory (
  input  [4:0] Write_Register,
  input  [4:0] Read_Register_B,
  input  [4:0] Read_Register_A,
  input  RegWrite,
  input  [31:0] WriteData,
  output [31:0] A,
  output [31:0] B
);

  wire and_1_out, and_2_out, and_3_out, and_4_out, and_5_out, and_6_out, and_7_out, and_8_out, and_9_out,
       and_10_out, and_11_out, and_12_out, and_13_out, and_14_out, and_15_out, and_16_out, and_17_out,
       and_18_out, and_19_out, and_20_out, and_21_out, and_22_out, and_23_out, and_24_out, and_25_out,
       and_26_out, and_27_out, and_28_out, and_29_out, and_30_out, and_31_out, and_32_out, clock_1_out,
       decoder_1_out0, decoder_1_out1, decoder_1_out2, decoder_1_out3, decoder_1_out4, decoder_1_out5,
       decoder_1_out6, decoder_1_out7, decoder_1_out8, decoder_1_out9, decoder_1_out10, decoder_1_out11,
       decoder_1_out12, decoder_1_out13, decoder_1_out14, decoder_1_out15, decoder_1_out16, decoder_1_out17,
       decoder_1_out18, decoder_1_out19, decoder_1_out20, decoder_1_out21, decoder_1_out22, decoder_1_out23,
       decoder_1_out24, decoder_1_out25, decoder_1_out26, decoder_1_out27, decoder_1_out28, decoder_1_out29,
       decoder_1_out30, decoder_1_out31;
  wire [31:0] register_1_q, register_2_q, register_3_q, register_4_q, register_5_q, register_6_q,
       register_7_q, register_8_q, register_9_q, register_10_q, register_11_q, register_12_q, register_13_q,
       register_14_q, register_15_q, register_16_q, register_17_q, register_18_q, register_19_q,
       register_20_q, register_21_q, register_22_q, register_23_q, register_24_q, register_25_q,
       register_26_q, register_27_q, register_28_q, register_29_q, register_30_q, register_31_q,
       register_32_q;

  Decoder #(.select(5)) decoder_1 (
    .out0(decoder_1_out0), .out1(decoder_1_out1), .out2(decoder_1_out2), .out3(decoder_1_out3),
    .out4(decoder_1_out4), .out5(decoder_1_out5), .out6(decoder_1_out6), .out7(decoder_1_out7),
    .out8(decoder_1_out8), .out9(decoder_1_out9), .out10(decoder_1_out10), .out11(decoder_1_out11),
    .out12(decoder_1_out12), .out13(decoder_1_out13), .out14(decoder_1_out14), .out15(decoder_1_out15),
    .out16(decoder_1_out16), .out17(decoder_1_out17), .out18(decoder_1_out18), .out19(decoder_1_out19),
    .out20(decoder_1_out20), .out21(decoder_1_out21), .out22(decoder_1_out22), .out23(decoder_1_out23),
    .out24(decoder_1_out24), .out25(decoder_1_out25), .out26(decoder_1_out26), .out27(decoder_1_out27),
    .out28(decoder_1_out28), .out29(decoder_1_out29), .out30(decoder_1_out30), .out31(decoder_1_out31),
    .sel(Write_Register));  // open: en
  and and_1 (and_1_out, decoder_1_out0, RegWrite);
  and and_2 (and_2_out, decoder_1_out1, RegWrite);
  and and_3 (and_3_out, decoder_1_out2, RegWrite);
  and and_4 (and_4_out, decoder_1_out3, RegWrite);
  and and_5 (and_5_out, decoder_1_out4, RegWrite);
  and and_6 (and_6_out, decoder_1_out5, RegWrite);
  and and_7 (and_7_out, decoder_1_out6, RegWrite);
  and and_8 (and_8_out, decoder_1_out7, RegWrite);
  and and_9 (and_9_out, decoder_1_out8, RegWrite);
  and and_10 (and_10_out, decoder_1_out9, RegWrite);
  and and_11 (and_11_out, decoder_1_out10, RegWrite);
  and and_12 (and_12_out, decoder_1_out11, RegWrite);
  and and_13 (and_13_out, decoder_1_out12, RegWrite);
  and and_14 (and_14_out, decoder_1_out13, RegWrite);
  and and_15 (and_15_out, decoder_1_out14, RegWrite);
  and and_16 (and_16_out, decoder_1_out15, RegWrite);
  and and_17 (and_17_out, decoder_1_out16, RegWrite);
  and and_18 (and_18_out, decoder_1_out17, RegWrite);
  and and_19 (and_19_out, decoder_1_out18, RegWrite);
  and and_20 (and_20_out, decoder_1_out19, RegWrite);
  and and_21 (and_21_out, decoder_1_out20, RegWrite);
  and and_22 (and_22_out, decoder_1_out21, RegWrite);
  and and_23 (and_23_out, decoder_1_out22, RegWrite);
  and and_24 (and_24_out, decoder_1_out23, RegWrite);
  and and_25 (and_25_out, decoder_1_out24, RegWrite);
  and and_26 (and_26_out, decoder_1_out25, RegWrite);
  and and_27 (and_27_out, decoder_1_out26, RegWrite);
  and and_28 (and_28_out, decoder_1_out27, RegWrite);
  and and_29 (and_29_out, decoder_1_out28, RegWrite);
  and and_30 (and_30_out, decoder_1_out29, RegWrite);
  and and_31 (and_31_out, decoder_1_out30, RegWrite);
  and and_32 (and_32_out, decoder_1_out31, RegWrite);
  Clock clock_1 (.out(clock_1_out));
  Register #(.width(32)) register_1 (.D({32{1'b0}}), .en(and_1_out), .Q(register_1_q), .clk(clock_1_out));  // open: clr
  Register #(.width(32)) register_2 (.D(WriteData), .en(and_2_out), .Q(register_2_q), .clk(clock_1_out));  // open: clr
  Register #(.width(32)) register_3 (.D(WriteData), .en(and_3_out), .Q(register_3_q), .clk(clock_1_out));  // open: clr
  Register #(.width(32)) register_4 (.D(WriteData), .en(and_4_out), .Q(register_4_q), .clk(clock_1_out));  // open: clr
  Register #(.width(32)) register_5 (.D(WriteData), .en(and_5_out), .Q(register_5_q), .clk(clock_1_out));  // open: clr
  Register #(.width(32)) register_6 (.D(WriteData), .en(and_6_out), .Q(register_6_q), .clk(clock_1_out));  // open: clr
  Register #(.width(32)) register_7 (.D(WriteData), .en(and_7_out), .Q(register_7_q), .clk(clock_1_out));  // open: clr
  Register #(.width(32)) register_8 (.D(WriteData), .en(and_8_out), .Q(register_8_q), .clk(clock_1_out));  // open: clr
  Register #(.width(32)) register_9 (.D(WriteData), .en(and_9_out), .Q(register_9_q), .clk(clock_1_out));  // open: clr
  Register #(.width(32)) register_10 (
    .D(WriteData), .en(and_10_out), .Q(register_10_q), .clk(clock_1_out));  // open: clr
  Register #(.width(32)) register_11 (
    .D(WriteData), .en(and_11_out), .Q(register_11_q), .clk(clock_1_out));  // open: clr
  Register #(.width(32)) register_12 (
    .D(WriteData), .en(and_12_out), .Q(register_12_q), .clk(clock_1_out));  // open: clr
  Register #(.width(32)) register_13 (
    .D(WriteData), .en(and_13_out), .Q(register_13_q), .clk(clock_1_out));  // open: clr
  Register #(.width(32)) register_14 (
    .D(WriteData), .en(and_14_out), .Q(register_14_q), .clk(clock_1_out));  // open: clr
  Register #(.width(32)) register_15 (
    .D(WriteData), .en(and_15_out), .Q(register_15_q), .clk(clock_1_out));  // open: clr
  Register #(.width(32)) register_16 (
    .D(WriteData), .en(and_16_out), .Q(register_16_q), .clk(clock_1_out));  // open: clr
  Register #(.width(32)) register_17 (
    .D(WriteData), .en(and_17_out), .Q(register_17_q), .clk(clock_1_out));  // open: clr
  Register #(.width(32)) register_18 (
    .D(WriteData), .en(and_18_out), .Q(register_18_q), .clk(clock_1_out));  // open: clr
  Register #(.width(32)) register_19 (
    .D(WriteData), .en(and_19_out), .Q(register_19_q), .clk(clock_1_out));  // open: clr
  Register #(.width(32)) register_20 (
    .D(WriteData), .en(and_20_out), .Q(register_20_q), .clk(clock_1_out));  // open: clr
  Register #(.width(32)) register_21 (
    .D(WriteData), .en(and_21_out), .Q(register_21_q), .clk(clock_1_out));  // open: clr
  Register #(.width(32)) register_22 (
    .D(WriteData), .en(and_22_out), .Q(register_22_q), .clk(clock_1_out));  // open: clr
  Register #(.width(32)) register_23 (
    .D(WriteData), .en(and_23_out), .Q(register_23_q), .clk(clock_1_out));  // open: clr
  Register #(.width(32)) register_24 (
    .D(WriteData), .en(and_24_out), .Q(register_24_q), .clk(clock_1_out));  // open: clr
  Register #(.width(32)) register_25 (
    .D(WriteData), .en(and_25_out), .Q(register_25_q), .clk(clock_1_out));  // open: clr
  Register #(.width(32)) register_26 (
    .D(WriteData), .en(and_26_out), .Q(register_26_q), .clk(clock_1_out));  // open: clr
  Register #(.width(32)) register_27 (
    .D(WriteData), .en(and_27_out), .Q(register_27_q), .clk(clock_1_out));  // open: clr
  Register #(.width(32)) register_28 (
    .D(WriteData), .en(and_28_out), .Q(register_28_q), .clk(clock_1_out));  // open: clr
  Register #(.width(32)) register_29 (
    .D(WriteData), .en(and_29_out), .Q(register_29_q), .clk(clock_1_out));  // open: clr
  Register #(.width(32)) register_30 (
    .D(WriteData), .en(and_30_out), .Q(register_30_q), .clk(clock_1_out));  // open: clr
  Register #(.width(32)) register_31 (
    .D(WriteData), .en(and_31_out), .Q(register_31_q), .clk(clock_1_out));  // open: clr
  Register #(.width(32)) register_32 (
    .D(WriteData), .en(and_32_out), .Q(register_32_q), .clk(clock_1_out));  // open: clr
  Multiplexer #(.select(5), .width(32)) multiplexer_1 (
    .in0(register_1_q), .in1(register_2_q), .in2(register_3_q), .in3(register_4_q), .in4(register_5_q),
    .in5(register_6_q), .in6(register_7_q), .in7(register_8_q), .in8(register_9_q), .in9(register_10_q),
    .in10(register_11_q), .in11(register_12_q), .in12(register_13_q), .in13(register_14_q),
    .in14(register_15_q), .in15(register_16_q), .in16(register_17_q), .in17(register_18_q),
    .in18(register_19_q), .in19(register_20_q), .in20(register_21_q), .in21(register_22_q),
    .in22(register_23_q), .in23(register_24_q), .in24(register_25_q), .in25(register_26_q),
    .in26(register_27_q), .in27(register_28_q), .in28(register_29_q), .in29(register_30_q),
    .in30(register_31_q), .in31(register_32_q), .out(A), .sel(Read_Register_A));  // open: en
  Multiplexer #(.select(5), .width(32)) multiplexer_2 (
    .in0(register_1_q), .in1(register_2_q), .in2(register_3_q), .in3(register_4_q), .in4(register_5_q),
    .in5(register_6_q), .in6(register_7_q), .in7(register_8_q), .in8(register_9_q), .in9(register_10_q),
    .in10(register_11_q), .in11(register_12_q), .in12(register_13_q), .in13(register_14_q),
    .in14(register_15_q), .in15(register_16_q), .in16(register_17_q), .in17(register_18_q),
    .in18(register_19_q), .in19(register_20_q), .in20(register_21_q), .in21(register_22_q),
    .in22(register_23_q), .in23(register_24_q), .in24(register_25_q), .in25(register_26_q),
    .in26(register_27_q), .in27(register_28_q), .in28(register_29_q), .in29(register_30_q),
    .in30(register_31_q), .in31(register_32_q), .out(B), .sel(Read_Register_B));  // open: en

  // Notes on the sheet:
  //   0x00
  //   0x01
  //   0x02
  //   0x03
  //   0x04
  //   0x05
  //   0x06
  //   0x07
  //   0x08
  //   0x09
  //   0x10
  //   0x11
  //   0x12
  //   0x13
  //   0x14
  //   0x15
  //   0x16
  //   0x17
  //   0x18
  //   0x19
  //   0x20
  //   0x21
  //   0x22
  //   0x23
  //   0x24
  //   0x25
  //   0x26
  //   0x27
  //   0x28
  //   0x29
  //   0x30
  //   0x31
  //   Register Memory
endmodule

module ControlLogic (
  input  [6:0] Opcode,
  output Branch,
  output LUI,
  output AUIPC,
  output JALR,
  output JAL,
  output Type_S,
  output MemWrite,
  output MemRead,
  output MemToReg,
  output RegWrite,
  output DataBSelect,
  output ImmSelect,
  output [4:0] ControlOp
);

  wire I_Type_out, or_1_out;

  and R_type (ControlOp[3], ~Opcode[6], Opcode[5], Opcode[4], ~Opcode[3], ~Opcode[2], Opcode[1], Opcode[0]);  // AND_Gate
  and Load (ControlOp[2], ~Opcode[6], ~Opcode[5], ~Opcode[4], ~Opcode[3], ~Opcode[2], Opcode[1], Opcode[0]);  // AND_Gate
  and S_Type (ControlOp[1], ~Opcode[6], Opcode[5], ~Opcode[4], ~Opcode[3], ~Opcode[2], Opcode[1], Opcode[0]);  // AND_Gate
  and I_Type (I_Type_out, ~Opcode[6], ~Opcode[5], Opcode[4], ~Opcode[3], ~Opcode[2], Opcode[1], Opcode[0]);  // AND_Gate
  or or_1 (or_1_out, I_Type_out, JAL);
  and u_JAL (JAL, Opcode[6], Opcode[5], ~Opcode[4], Opcode[3], Opcode[2], Opcode[1], Opcode[0]);  // AND_Gate
  and u_JALR (JALR, Opcode[6], Opcode[5], ~Opcode[4], ~Opcode[3], Opcode[2], Opcode[1], Opcode[0]);  // AND_Gate
  and u_AUIPC (AUIPC, ~Opcode[6], ~Opcode[5], Opcode[4], ~Opcode[3], Opcode[2], Opcode[1], Opcode[0]);  // AND_Gate
  and u_LUI (LUI, ~Opcode[6], Opcode[5], Opcode[4], ~Opcode[3], Opcode[2], Opcode[1], Opcode[0]);  // AND_Gate
  and u_Branch (Branch, Opcode[6], Opcode[5], ~Opcode[4], ~Opcode[3], ~Opcode[2], Opcode[1], Opcode[0]);  // AND_Gate
  or or_2 (ControlOp[0], JALR, or_1_out);
  or or_3 (RegWrite, LUI, AUIPC, JALR, JAL, or_1_out, ControlOp[2], ControlOp[3]);
  or or_4 (DataBSelect, JALR, or_1_out, ControlOp[1], ControlOp[2]);

  assign ControlOp[4] = Branch;
  assign ImmSelect = ControlOp[0];
  assign MemRead = ControlOp[2];
  assign MemToReg = ControlOp[2];
  assign MemWrite = ControlOp[1];
  assign Type_S = ControlOp[1];

  // Notes on the sheet:
  //   Control Logic
endmodule

module FuctionLogic (
  input  [2:0] ALUFunction,
  input  [6:0] FunctionCode,
  input  [4:0] ControlOp,
  output Sub_EN,
  output [2:0] LoadSelect,
  output [1:0] StoreSelect,
  output [3:0] ALUOp
);

  wire ADD_out, LH_out, LW_out, or_1_out, or_2_out, or_3_out, OR_4_out, priority_encoder_1_p1,
       priority_encoder_1_p3, priority_encoder_1_p5, priority_encoder_1_p6, priority_encoder_1_p7,
       priority_encoder_1_p10, priority_encoder_1_p11, priority_encoder_1_p12, priority_encoder_1_p13,
       priority_encoder_1_p14, priority_encoder_1_p15, priority_encoder_2_p3, priority_encoder_2_p4,
       priority_encoder_2_p6, priority_encoder_3_p4, SH_out, SUB_out, SW_out;

  or or_1 (or_1_out, ControlOp[3], ControlOp[0]);
  and and_1 (Sub_EN, ControlOp[3], SUB_out);
  and ADD (ADD_out, ~FunctionCode[5], ~ALUFunction[2], or_1_out, ~ALUFunction[1], ~ALUFunction[0]);  // AND_Gate
  or or_2 (or_2_out, ControlOp[2], ControlOp[1], ADD_out);
  or or_3 (or_3_out, or_2_out, SUB_out);
  and OR_4 (OR_4_out, ALUFunction[2], ALUFunction[1], ~ALUFunction[0]);  // AND_Gate
  and SUB (SUB_out, FunctionCode[5], ~ALUFunction[2], ~ALUFunction[1], ~ALUFunction[0]);  // AND_Gate
  // Priority_Encoder #(.select(4)) priority_encoder_1: pin names not known; wires that end beside it: priority_encoder_1_p1, OR_4_out, priority_encoder_1_p3, or_3_out, priority_encoder_1_p5, priority_encoder_1_p6, priority_encoder_1_p7, ControlOp[4], ALUOp, priority_encoder_1_p10, priority_encoder_1_p11, priority_encoder_1_p12, priority_encoder_1_p13, priority_encoder_1_p14, priority_encoder_1_p15
  and AND_2 (priority_encoder_1_p1, ALUFunction[2], ALUFunction[1], ALUFunction[0]);
  and SLL (priority_encoder_1_p5, ~ALUFunction[2], ~ALUFunction[1], ALUFunction[0]);  // AND_Gate
  and XOR (priority_encoder_1_p3, ALUFunction[2], ~ALUFunction[1], ~ALUFunction[0]);  // AND_Gate
  and SRL (priority_encoder_1_p6, ~FunctionCode[5], ALUFunction[2], ~ALUFunction[1], ALUFunction[0]);  // AND_Gate
  and SRA (priority_encoder_1_p7, FunctionCode[5], ALUFunction[2], ~ALUFunction[1], ALUFunction[0]);  // AND_Gate
  and SLTU (priority_encoder_1_p11, ~ALUFunction[2], ALUFunction[1], ALUFunction[0]);  // AND_Gate
  and SLT (priority_encoder_1_p10, ~ALUFunction[2], ALUFunction[1], ~ALUFunction[0]);  // AND_Gate
  and BLT (priority_encoder_1_p12, ControlOp[4], ALUFunction[2], ~ALUFunction[1], ~ALUFunction[0]);  // AND_Gate
  and BLTU (priority_encoder_1_p13, ControlOp[4], ALUFunction[2], ALUFunction[1], ~ALUFunction[0]);  // AND_Gate
  and BGE (priority_encoder_1_p14, ControlOp[4], ALUFunction[2], ~ALUFunction[1], ALUFunction[0]);  // AND_Gate
  and LW (LW_out, ~ALUFunction[2], ALUFunction[1], ~ALUFunction[0]);  // AND_Gate
  and BGEU (priority_encoder_1_p15, ControlOp[4], ALUFunction[2], ALUFunction[1], ALUFunction[0]);
  and LH (LH_out, ~ALUFunction[2], ~ALUFunction[1], ALUFunction[0]);  // AND_Gate
  // Priority_Encoder priority_encoder_2: pin names not known; wires that end beside it: LW_out, LH_out, priority_encoder_2_p3, priority_encoder_2_p4, LoadSelect, priority_encoder_2_p6
  and LB (priority_encoder_2_p3, ~ALUFunction[2], ~ALUFunction[1], ~ALUFunction[0]);  // AND_Gate
  and LHU (priority_encoder_2_p4, ALUFunction[2], ~ALUFunction[1], ALUFunction[0]);  // AND_Gate
  and LBU (priority_encoder_2_p6, ALUFunction[2], ~ALUFunction[1], ~ALUFunction[0]);  // AND_Gate
  and SH (SH_out, ~ALUFunction[2], ~ALUFunction[1], ALUFunction[0]);  // AND_Gate
  and SW (SW_out, ~ALUFunction[2], ALUFunction[1], ~ALUFunction[0]);  // AND_Gate
  // Priority_Encoder #(.select(2)) priority_encoder_3: pin names not known; wires that end beside it: SW_out, SH_out, StoreSelect, priority_encoder_3_p4
  and SB (priority_encoder_3_p4, ~ALUFunction[2], ~ALUFunction[1], ~ALUFunction[0]);  // AND_Gate

  // Notes on the sheet:
  //   Function Logic
endmodule

module _32BitALU (
  input  [31:0] A,
  input  [3:0] ALUOp,
  input  Sub_EN,
  input  [31:0] B,
  output Zero,
  output [31:0] Output,
  output Overflow
);

  wire and_1_out, and_2_out, and_3_out, and_4_out, and_5_out, and_6_out, and_7_out, and_8_out, and_9_out,
       and_10_out, comparator_1_eq, comparator_1_gt, comparator_1_lt, comparator_2_eq, comparator_2_gt,
       comparator_2_lt, n1bitalu_1_cout, n1bitalu_2_cout, n1bitalu_3_cout, n1bitalu_4_cout, n1bitalu_5_cout,
       n1bitalu_6_cout, n1bitalu_7_cout, n1bitalu_8_cout, n1bitalu_9_cout, n1bitalu_10_cout,
       n1bitalu_11_cout, n1bitalu_12_cout, n1bitalu_13_cout, n1bitalu_14_cout, n1bitalu_15_cout,
       n1bitalu_16_cout, n1bitalu_17_cout, n1bitalu_18_cout, n1bitalu_19_cout, n1bitalu_20_cout,
       n1bitalu_21_cout, n1bitalu_22_cout, n1bitalu_23_cout, n1bitalu_24_cout, n1bitalu_25_cout,
       n1bitalu_26_cout, n1bitalu_27_cout, n1bitalu_28_cout, n1bitalu_29_cout, n1bitalu_30_cout,
       n1bitalu_31_cout, n1bitalu_32_set, or_1_out, or_2_out, or_3_out, or_4_out;
  wire [2:0] priority_encoder_1_out;
  wire [31:0] bit_extender_1_out, bit_extender_2_out, bit_extender_3_out, bit_extender_4_out,
       n1bitalu_1_output, shifter_1_out, shifter_2_out, shifter_3_out;

  and and_1 (and_1_out, Sub_EN, 1'b1);
  _1BitALU u_1bitalu_1 (
    .A(A[0]), .B(B[0]), .Less(n1bitalu_32_set), .Output(n1bitalu_1_output[0]), .Cin(and_1_out),
    .Sub_EN(Sub_EN), .Cout(n1bitalu_1_cout), .ALU_Operation(ALUOp));  // open: Set
  _1BitALU u_1bitalu_2 (
    .A(A[1]), .B(B[1]), .Less(1'b0), .Output(n1bitalu_1_output[1]), .Cin(n1bitalu_1_cout), .Sub_EN(Sub_EN),
    .Cout(n1bitalu_2_cout), .ALU_Operation(ALUOp));  // open: Set
  _1BitALU u_1bitalu_3 (
    .A(A[2]), .B(B[2]), .Less(1'b0), .Output(n1bitalu_1_output[2]), .Cin(n1bitalu_2_cout), .Sub_EN(Sub_EN),
    .Cout(n1bitalu_3_cout), .ALU_Operation(ALUOp));  // open: Set
  _1BitALU u_1bitalu_4 (
    .A(A[3]), .B(B[3]), .Less(1'b0), .Output(n1bitalu_1_output[3]), .Cin(n1bitalu_3_cout), .Sub_EN(Sub_EN),
    .Cout(n1bitalu_4_cout), .ALU_Operation(ALUOp));  // open: Set
  _1BitALU u_1bitalu_5 (
    .A(A[4]), .B(B[4]), .Less(1'b0), .Output(n1bitalu_1_output[4]), .Cin(n1bitalu_4_cout), .Sub_EN(Sub_EN),
    .Cout(n1bitalu_5_cout), .ALU_Operation(ALUOp));  // open: Set
  _1BitALU u_1bitalu_6 (
    .A(A[5]), .B(B[5]), .Less(1'b0), .Output(n1bitalu_1_output[5]), .Cin(n1bitalu_5_cout), .Sub_EN(Sub_EN),
    .Cout(n1bitalu_6_cout), .ALU_Operation(ALUOp));  // open: Set
  _1BitALU u_1bitalu_7 (
    .A(A[6]), .B(B[6]), .Less(1'b0), .Output(n1bitalu_1_output[6]), .Cin(n1bitalu_6_cout), .Sub_EN(Sub_EN),
    .Cout(n1bitalu_7_cout), .ALU_Operation(ALUOp));  // open: Set
  _1BitALU u_1bitalu_8 (
    .A(A[7]), .B(B[7]), .Less(1'b0), .Output(n1bitalu_1_output[7]), .Cin(n1bitalu_7_cout), .Sub_EN(Sub_EN),
    .Cout(n1bitalu_8_cout), .ALU_Operation(ALUOp));  // open: Set
  _1BitALU u_1bitalu_9 (
    .A(A[8]), .B(B[8]), .Less(1'b0), .Output(n1bitalu_1_output[8]), .Cin(n1bitalu_8_cout), .Sub_EN(Sub_EN),
    .Cout(n1bitalu_9_cout), .ALU_Operation(ALUOp));  // open: Set
  _1BitALU u_1bitalu_10 (
    .A(A[9]), .B(B[9]), .Less(1'b0), .Output(n1bitalu_1_output[9]), .Cin(n1bitalu_9_cout), .Sub_EN(Sub_EN),
    .Cout(n1bitalu_10_cout), .ALU_Operation(ALUOp));  // open: Set
  _1BitALU u_1bitalu_11 (
    .A(A[10]), .B(B[10]), .Less(1'b0), .Output(n1bitalu_1_output[10]), .Cin(n1bitalu_10_cout),
    .Sub_EN(Sub_EN), .Cout(n1bitalu_11_cout), .ALU_Operation(ALUOp));  // open: Set
  _1BitALU u_1bitalu_12 (
    .A(A[11]), .B(B[11]), .Less(1'b0), .Output(n1bitalu_1_output[11]), .Cin(n1bitalu_11_cout),
    .Sub_EN(Sub_EN), .Cout(n1bitalu_12_cout), .ALU_Operation(ALUOp));  // open: Set
  _1BitALU u_1bitalu_13 (
    .A(A[12]), .B(B[12]), .Less(1'b0), .Output(n1bitalu_1_output[12]), .Cin(n1bitalu_12_cout),
    .Sub_EN(Sub_EN), .Cout(n1bitalu_13_cout), .ALU_Operation(ALUOp));  // open: Set
  _1BitALU u_1bitalu_14 (
    .A(A[13]), .B(B[13]), .Less(1'b0), .Output(n1bitalu_1_output[13]), .Cin(n1bitalu_13_cout),
    .Sub_EN(Sub_EN), .Cout(n1bitalu_14_cout), .ALU_Operation(ALUOp));  // open: Set
  _1BitALU u_1bitalu_15 (
    .A(A[14]), .B(B[14]), .Less(1'b0), .Output(n1bitalu_1_output[14]), .Cin(n1bitalu_14_cout),
    .Sub_EN(Sub_EN), .Cout(n1bitalu_15_cout), .ALU_Operation(ALUOp));  // open: Set
  _1BitALU u_1bitalu_16 (
    .A(A[15]), .B(B[15]), .Less(1'b0), .Output(n1bitalu_1_output[15]), .Cin(n1bitalu_15_cout),
    .Sub_EN(Sub_EN), .Cout(n1bitalu_16_cout), .ALU_Operation(ALUOp));  // open: Set
  _1BitALU u_1bitalu_17 (
    .A(A[16]), .B(B[16]), .Less(1'b0), .Output(n1bitalu_1_output[16]), .Cin(n1bitalu_16_cout),
    .Sub_EN(Sub_EN), .Cout(n1bitalu_17_cout), .ALU_Operation(ALUOp));  // open: Set
  _1BitALU u_1bitalu_18 (
    .A(A[17]), .B(B[17]), .Less(1'b0), .Output(n1bitalu_1_output[17]), .Cin(n1bitalu_17_cout),
    .Sub_EN(Sub_EN), .Cout(n1bitalu_18_cout), .ALU_Operation(ALUOp));  // open: Set
  _1BitALU u_1bitalu_19 (
    .A(A[18]), .B(B[18]), .Less(1'b0), .Output(n1bitalu_1_output[18]), .Cin(n1bitalu_18_cout),
    .Sub_EN(Sub_EN), .Cout(n1bitalu_19_cout), .ALU_Operation(ALUOp));  // open: Set
  _1BitALU u_1bitalu_20 (
    .A(A[19]), .B(B[19]), .Less(1'b0), .Output(n1bitalu_1_output[19]), .Cin(n1bitalu_19_cout),
    .Sub_EN(Sub_EN), .Cout(n1bitalu_20_cout), .ALU_Operation(ALUOp));  // open: Set
  _1BitALU u_1bitalu_21 (
    .A(A[20]), .B(B[20]), .Less(1'b0), .Output(n1bitalu_1_output[20]), .Cin(n1bitalu_20_cout),
    .Sub_EN(Sub_EN), .Cout(n1bitalu_21_cout), .ALU_Operation(ALUOp));  // open: Set
  _1BitALU u_1bitalu_22 (
    .A(A[21]), .B(B[21]), .Less(1'b0), .Output(n1bitalu_1_output[21]), .Cin(n1bitalu_21_cout),
    .Sub_EN(Sub_EN), .Cout(n1bitalu_22_cout), .ALU_Operation(ALUOp));  // open: Set
  _1BitALU u_1bitalu_23 (
    .A(A[22]), .B(B[22]), .Less(1'b0), .Output(n1bitalu_1_output[22]), .Cin(n1bitalu_22_cout),
    .Sub_EN(Sub_EN), .Cout(n1bitalu_23_cout), .ALU_Operation(ALUOp));  // open: Set
  _1BitALU u_1bitalu_24 (
    .A(A[23]), .B(B[23]), .Less(1'b0), .Output(n1bitalu_1_output[23]), .Cin(n1bitalu_23_cout),
    .Sub_EN(Sub_EN), .Cout(n1bitalu_24_cout), .ALU_Operation(ALUOp));  // open: Set
  _1BitALU u_1bitalu_25 (
    .A(A[24]), .B(B[24]), .Less(1'b0), .Output(n1bitalu_1_output[24]), .Cin(n1bitalu_24_cout),
    .Sub_EN(Sub_EN), .Cout(n1bitalu_25_cout), .ALU_Operation(ALUOp));  // open: Set
  _1BitALU u_1bitalu_26 (
    .A(A[25]), .B(B[25]), .Less(1'b0), .Output(n1bitalu_1_output[25]), .Cin(n1bitalu_25_cout),
    .Sub_EN(Sub_EN), .Cout(n1bitalu_26_cout), .ALU_Operation(ALUOp));  // open: Set
  _1BitALU u_1bitalu_27 (
    .A(A[26]), .B(B[26]), .Less(1'b0), .Output(n1bitalu_1_output[26]), .Cin(n1bitalu_26_cout),
    .Sub_EN(Sub_EN), .Cout(n1bitalu_27_cout), .ALU_Operation(ALUOp));  // open: Set
  _1BitALU u_1bitalu_28 (
    .A(A[27]), .B(B[27]), .Less(1'b0), .Output(n1bitalu_1_output[27]), .Cin(n1bitalu_27_cout),
    .Sub_EN(Sub_EN), .Cout(n1bitalu_28_cout), .ALU_Operation(ALUOp));  // open: Set
  _1BitALU u_1bitalu_29 (
    .A(A[28]), .B(B[28]), .Less(1'b0), .Output(n1bitalu_1_output[28]), .Cin(n1bitalu_28_cout),
    .Sub_EN(Sub_EN), .Cout(n1bitalu_29_cout), .ALU_Operation(ALUOp));  // open: Set
  _1BitALU u_1bitalu_30 (
    .A(A[29]), .B(B[29]), .Less(1'b0), .Output(n1bitalu_1_output[29]), .Cin(n1bitalu_29_cout),
    .Sub_EN(Sub_EN), .Cout(n1bitalu_30_cout), .ALU_Operation(ALUOp));  // open: Set
  _1BitALU u_1bitalu_31 (
    .A(A[30]), .B(B[30]), .Less(1'b0), .Output(n1bitalu_1_output[30]), .Cin(n1bitalu_30_cout),
    .Sub_EN(Sub_EN), .Cout(n1bitalu_31_cout), .ALU_Operation(ALUOp));  // open: Set
  _1BitALU u_1bitalu_32 (
    .A(A[31]), .B(B[31]), .Less(1'b0), .Output(n1bitalu_1_output[31]), .Set(n1bitalu_32_set),
    .Cin(n1bitalu_31_cout), .Sub_EN(Sub_EN), .Cout(Overflow), .ALU_Operation(ALUOp));
  Comparator #(.width(32), .mode("unsigned")) comparator_1 (
    .a(A), .b(B), .gt(comparator_1_gt), .eq(comparator_1_eq), .lt(comparator_1_lt));
  Comparator #(.width(32)) comparator_2 (
    .a(A), .b(B), .gt(comparator_2_gt), .eq(comparator_2_eq), .lt(comparator_2_lt));
  Shifter #(.width(32), .shift("ar")) shifter_1 (.in(A), .\dist (B[4:0]), .out(shifter_1_out));
  Shifter #(.width(32), .shift("lr")) shifter_2 (.in(A), .\dist (B[4:0]), .out(shifter_2_out));
  Shifter #(.width(32)) shifter_3 (.in(A), .\dist (B[4:0]), .out(shifter_3_out));
  or or_1 (or_1_out, comparator_1_gt, comparator_1_eq);
  assign bit_extender_1_out = {{31{1'b0}}, comparator_1_lt};  // Bit_Extender bit_extender_1
  or or_2 (or_2_out, comparator_2_gt, comparator_2_eq);
  assign bit_extender_2_out = {{31{1'b0}}, comparator_2_lt};  // Bit_Extender bit_extender_2
  assign bit_extender_3_out = {{31{1'b0}}, or_1_out};  // Bit_Extender bit_extender_3
  assign bit_extender_4_out = {{31{1'b0}}, or_2_out};  // Bit_Extender bit_extender_4
  and and_2 (and_2_out, ALUOp[3], ~ALUOp[2], ALUOp[1], ALUOp[0]);  // AND_Gate
  and and_3 (and_3_out, ALUOp[3], ~ALUOp[2], ALUOp[1], ~ALUOp[0]);  // AND_Gate
  or or_3 (or_3_out, and_2_out, and_4_out);
  and and_4 (and_4_out, ALUOp[3], ~ALUOp[2], ~ALUOp[1], ALUOp[0]);  // AND_Gate
  nor nor_1 (Zero, n1bitalu_1_output[0], n1bitalu_1_output[1], n1bitalu_1_output[2], n1bitalu_1_output[3], n1bitalu_1_output[4], n1bitalu_1_output[5], n1bitalu_1_output[6], n1bitalu_1_output[7], n1bitalu_1_output[8], n1bitalu_1_output[9], n1bitalu_1_output[10], n1bitalu_1_output[11], n1bitalu_1_output[12], n1bitalu_1_output[13], n1bitalu_1_output[14], n1bitalu_1_output[15], n1bitalu_1_output[16], n1bitalu_1_output[17], n1bitalu_1_output[18], n1bitalu_1_output[19], n1bitalu_1_output[20], n1bitalu_1_output[21], n1bitalu_1_output[22], n1bitalu_1_output[23], n1bitalu_1_output[24], n1bitalu_1_output[25], n1bitalu_1_output[26], n1bitalu_1_output[27], n1bitalu_1_output[28], n1bitalu_1_output[29], n1bitalu_1_output[30], n1bitalu_1_output[31]);
  or or_4 (or_4_out, and_3_out, and_5_out);
  and and_5 (and_5_out, ALUOp[3], ~ALUOp[2], ~ALUOp[1], ~ALUOp[0]);  // AND_Gate
  Priority_Encoder priority_encoder_1 (
    .in0(1'b1), .in1(and_8_out), .in2(and_7_out), .in3(and_6_out), .in4(or_4_out), .in5(or_3_out),
    .in6(and_9_out), .in7(and_10_out), .out(priority_encoder_1_out));  // open: en_in
  and and_6 (and_6_out, ~ALUOp[3], ALUOp[2], ALUOp[1], ~ALUOp[0]);  // AND_Gate
  Multiplexer #(.select(3), .width(32)) multiplexer_1 (
    .in0(n1bitalu_1_output), .in1(shifter_2_out), .in2(shifter_3_out), .in3(shifter_1_out),
    .in4(bit_extender_2_out), .in5(bit_extender_1_out), .in6(bit_extender_4_out), .in7(bit_extender_3_out),
    .out(Output), .sel(priority_encoder_1_out));  // open: en
  and and_7 (and_7_out, ~ALUOp[3], ALUOp[2], ~ALUOp[1], ALUOp[0]);  // AND_Gate
  and and_8 (and_8_out, ~ALUOp[3], ALUOp[2], ~ALUOp[1], ~ALUOp[0]);  // AND_Gate
  and and_9 (and_9_out, ALUOp[3], ALUOp[2], ~ALUOp[1], ~ALUOp[0]);  // AND_Gate
  and and_10 (and_10_out, ALUOp[3], ALUOp[2], ~ALUOp[1], ALUOp[0]);  // AND_Gate

  // Notes on the sheet:
  //   CompareU
  //   Compare
  //   SRA
  //   SLR
  //   SLL
  //   32-Bit ALU
  //   BLTU Check
  //   BLT Check
  //   SLTU Check
  //   SLT Check
  //   SRA Check
  //   SRL Check
  //   SLL Check
  //   BGE Check
  //   BGEU Check
endmodule

module _1BitALU (
  input  Cin,
  input  A,
  input  B,
  input  Less,
  input  Sub_EN,
  input  [3:0] ALU_Operation,
  output Output,
  output Set,
  output Cout
);

  wire and_1_out, multiplexer_1_out, not_1_out, or_1_out, xnor_1_out, xor_1_out;

  not not_1 (not_1_out, B);
  Multiplexer multiplexer_1 (.in0(B), .in1(not_1_out), .out(multiplexer_1_out), .sel(Sub_EN));  // open: en
  Adder #(.width(1)) adder_1 (.a(A), .b(multiplexer_1_out), .out(Set), .cin(Cin), .cout(Cout));
  and and_1 (and_1_out, A, B);
  or or_1 (or_1_out, A, B);
  xor xor_1 (xor_1_out, A, B);
  xnor xnor_1 (xnor_1_out, A, B);
  Multiplexer #(.select(4)) multiplexer_2 (
    .in0(and_1_out), .in1(or_1_out), .in2(xor_1_out), .in3(Set), .in5(Less), .in7(xnor_1_out), .out(Output),
    .sel(ALU_Operation));  // open: in4, in6, in8, in9, in10, in11, in12, in13, in14, in15, en

  // Notes on the sheet:
  //   1-Bit ALU
endmodule

module ImmediateGen (
  input  [24:0] Imm25Bit,
  input  Type_S,
  input  ImmSelect,
  output [31:0] Imm32Bit
);

  wire [4:0] multiplexer_1_out;
  wire [31:0] bit_extender_1_out, bit_extender_2_out;

  Multiplexer #(.width(5)) multiplexer_1 (
    .in0(Imm25Bit[17:13]), .in1(Imm25Bit[4:0]), .out(multiplexer_1_out), .sel(Type_S));  // open: en
  // Probe on {Imm25Bit[24:18], multiplexer_1_out}
  assign bit_extender_1_out = {{20{1'b0}}, {Imm25Bit[24:18], multiplexer_1_out}};  // Bit_Extender bit_extender_1
  assign bit_extender_2_out = {{20{Imm25Bit[24]}}, {Imm25Bit[24:18], multiplexer_1_out}};  // Bit_Extender bit_extender_2
  Multiplexer #(.width(32)) multiplexer_2 (
    .in0(bit_extender_1_out), .in1(bit_extender_2_out), .out(Imm32Bit), .sel(ImmSelect));  // open: en

  // Notes on the sheet:
  //   Immediate Generator
endmodule

module ProgramCounter (
  input  [24:0] ImmCode,
  input  [31:0] ALUData,
  input  JALR,
  input  Branch,
  input  JAL,
  input  AUPIC,
  output [23:0] Instruction_Count,
  output [31:0] NextInstCount,
  output WMux
);

  wire and_1_out, BEQ_out, BGE_2_out, BGE_out, BLT_out, BLTU_out, BNE_out, Branch_out, clock_1_out, or_1_out,
       or_2_out, or_3_out;
  wire [11:0] shifter_1_out;
  wire [19:0] shifter_2_out;
  wire [31:0] adder_1_out, bit_extender_1_out, bit_extender_2_out, bit_extender_3_out, multiplexer_1_out,
       multiplexer_2_out, multiplexer_3_out, multiplexer_4_out, register_2_q;
  wire [31:24] register_1_q;

  Shifter #(.width(12)) shifter_1 (
    .in({ImmCode[24], ImmCode[0], ImmCode[23:18], ImmCode[4:1]}), .\dist (4'b0001), .out(shifter_1_out));
  Shifter #(.width(20)) shifter_2 (
    .in({ImmCode[24], ImmCode[12:5], ImmCode[13], ImmCode[23:14]}), .\dist (5'b00001), .out(shifter_2_out));
  assign bit_extender_1_out = {{20{shifter_1_out[11]}}, shifter_1_out};  // Bit_Extender bit_extender_1
  and u_Branch (Branch_out, ALUData[0], ALUData[1], ALUData[2], ALUData[3], ALUData[4], ALUData[5], ALUData[6], ALUData[7], ALUData[8], ALUData[9], ALUData[10], ALUData[11], ALUData[12], ALUData[13], ALUData[14], ALUData[15], ALUData[16], ALUData[17], ALUData[18], ALUData[19], ALUData[20], ALUData[21], ALUData[22], ALUData[23], ALUData[24], ALUData[25], ALUData[26], ALUData[27], ALUData[28], ALUData[29], ALUData[30], ALUData[31]);
  assign bit_extender_2_out = {{12{shifter_2_out[19]}}, shifter_2_out};  // Bit_Extender bit_extender_2
  or or_1 (or_1_out, BEQ_out, BNE_out, BLT_out, BLTU_out, BGE_out, BGE_2_out);
  and BEQ (BEQ_out, ~ImmCode[5], ~ImmCode[6], ~ImmCode[7], Branch_out);  // AND_Gate
  and BNE (BNE_out, ImmCode[5], ~ImmCode[6], ~ImmCode[7], ~Branch_out);  // AND_Gate
  and BLT (BLT_out, ImmCode[7], ~ImmCode[6], ~ImmCode[5], ALUData[0]);  // AND_Gate
  and BLTU (BLTU_out, ImmCode[7], ImmCode[6], ~ImmCode[5], ALUData[0]);  // AND_Gate
  and BGE (BGE_out, ImmCode[5], ~ImmCode[6], ImmCode[7], ALUData[0]);  // AND_Gate
  and BGE_2 (BGE_2_out, ImmCode[5], ImmCode[6], ImmCode[7], ALUData[0]);
  Multiplexer #(.width(32)) multiplexer_1 (
    .in0(bit_extender_2_out), .in1(bit_extender_1_out), .out(multiplexer_1_out), .sel(or_1_out));  // open: en
  Multiplexer #(.width(32)) multiplexer_2 (
    .in0(multiplexer_1_out), .in1(ALUData), .out(multiplexer_2_out), .sel(JALR));  // open: en
  assign bit_extender_3_out = {{12{1'b0}}, ImmCode[24:5]};  // Bit_Extender bit_extender_3
  Multiplexer #(.width(32)) multiplexer_3 (
    .in0(32'h1), .in1(multiplexer_2_out), .out(multiplexer_3_out), .sel(or_2_out));  // open: en
  Clock clock_1 (.out(clock_1_out));
  or or_2 (or_2_out, JALR, and_1_out, JAL);
  and and_1 (and_1_out, or_1_out, Branch);
  Register #(.width(32), .trigger("falling")) register_1 (
    .D(adder_1_out), .Q({register_1_q, Instruction_Count}), .clk(clock_1_out));  // open: en, clr
  or or_3 (or_3_out, or_2_out, AUPIC);
  or or_4 (WMux, JAL, AUPIC);
  Adder #(.width(32)) adder_1 (
    .a(multiplexer_3_out), .b({register_1_q, Instruction_Count}), .out(adder_1_out));  // open: cin, cout
  Register #(.width(32)) register_2 (
    .D({register_1_q, Instruction_Count}), .Q(register_2_q), .clk(or_3_out));  // open: en, clr
  Multiplexer #(.width(32)) multiplexer_4 (
    .in0(32'h1), .in1(bit_extender_3_out), .out(multiplexer_4_out), .sel(AUPIC));  // open: en
  Adder #(.width(32)) adder_2 (.a(register_2_q), .b(multiplexer_4_out), .out(NextInstCount));  // open: cin, cout

  // Notes on the sheet:
  //   Branch
  //   JAL
  //   Program Counter
  //   AUPIC
  //   PC Next Value to Rd
endmodule

module DataSelect (
  input  WMux,
  input  [31:0] ALUData,
  input  [31:0] NextInstCount,
  input  [31:0] InstCode,
  input  LUI,
  output [31:0] Data_W
);

  wire [31:0] multiplexer_1_out;

  Multiplexer #(.width(32)) multiplexer_1 (
    .in0(ALUData), .in1(NextInstCount), .out(multiplexer_1_out), .sel(WMux));  // open: en
  Multiplexer #(.width(32)) multiplexer_2 (
    .in0(multiplexer_1_out), .in1({InstCode[31:12], {12{1'b0}}}), .out(Data_W), .sel(LUI));  // open: en

  // Notes on the sheet:
  //   Data Write Select
endmodule

module LoadType (
  input  [31:0] DMem,
  input  [2:0] LoadSel,
  output [31:0] DataW
);

  wire [31:0] bit_extender_1_out, bit_extender_2_out, bit_extender_3_out, bit_extender_4_out;

  assign bit_extender_1_out = {{16{DMem[15]}}, DMem[15:0]};  // Bit_Extender bit_extender_1
  assign bit_extender_2_out = {{24{DMem[7]}}, DMem[7:0]};  // Bit_Extender bit_extender_2
  assign bit_extender_3_out = {{16{1'b0}}, DMem[15:0]};  // Bit_Extender bit_extender_3
  assign bit_extender_4_out = {{24{DMem[7]}}, DMem[7:0]};  // Bit_Extender bit_extender_4
  Multiplexer #(.select(3), .width(32)) multiplexer_1 (
    .in0(DMem), .in1(bit_extender_1_out), .in2(bit_extender_2_out), .in3(bit_extender_3_out),
    .in4(bit_extender_4_out), .out(DataW), .sel(LoadSel));  // open: in5, in6, in7, en

  // Notes on the sheet:
  //   Load Data Type Select
endmodule

module StoreType (
  input  [31:0] Data_rs2,
  input  [1:0] StoreSel,
  output [31:0] MemD
);

  wire [31:0] bit_extender_1_out, bit_extender_2_out;

  assign bit_extender_1_out = {{16{1'b0}}, Data_rs2[15:0]};  // Bit_Extender bit_extender_1
  assign bit_extender_2_out = {{24{1'b0}}, Data_rs2[7:0]};  // Bit_Extender bit_extender_2
  Multiplexer #(.select(2), .width(32)) multiplexer_1 (
    .in0(Data_rs2), .in1(bit_extender_1_out), .in2(bit_extender_2_out), .out(MemD), .sel(StoreSel));  // open: in3, en

  // Notes on the sheet:
  //   Store Data Type Select
endmodule
